// Logisim project A4.circ as structural Verilog: 3 circuits, main circuit main
module main (
  input  in_1,
  input  in_2,
  input  in_3,
  input  in_4,
  input  [31:0] in_5,
  input  in_6,
  input  in_7,
  input  in_8,
  input  in_9,
  input  [31:0] in_10,
  input  [31:0] in_11,
  input  [1:0] in_12,
  input  in_13,
  output [31:0] out_14,
  output [31:0] out_15,
  output [31:0] out_16
);

  wire clk;
  wire [2:0] selectRA, selectRB, selectRY;
  wire [31:0] registerfile_1_ra, registerfile_1_rb;

  RegisterFile registerfile_1 (
    .RA(registerfile_1_ra), .Address_RA(selectRA), .Address_RY(selectRY), .RB(registerfile_1_rb),
    .Address_RB(selectRB), .RY(in_5), .clk(clk), .enRA(in_2), .enRB(in_3), .enRY(in_4), .clr(in_1));
  Register #(.width(32)) RA (.D(registerfile_1_ra), .en(in_6), .Q(out_14), .clk(clk), .clr(in_8));
  ALU alu_1 (.ALU_Out(out_16), .ALU_Enable(in_13), .InputRA(in_10), .InputRB(in_11), .ALU_Select(in_12));
  Register #(.width(32)) RB (.D(registerfile_1_rb), .en(in_7), .Q(out_15), .clk(clk), .clr(in_9));
  Clock clock_1 (.out(clk));

  // Other names for the same wires on the sheet: ALU_Enable = in_13; ALU_Out[31:0] = out_16; ALU_Select[1:0] = in_12;
  //   clr = in_1; clrRA = in_8; clrRB = in_9; enRA = in_6; enRB = in_7; enSelectRA = in_2; enSelectRB = in_3;
  //   enSelectRY = in_4; InputRA[31:0] = in_10; InputRB[31:0] = in_11; OutRA[31:0] = out_14; OutRB[31:0] = out_15;
  //   RY[31:0] = in_5

  // Notes on the sheet:
  //   19CS01065
  //   Main File
endmodule

module RegisterFile (
  input  enRA,
  input  [2:0] Address_RA,
  input  enRY,
  input  [2:0] Address_RY,
  input  enRB,
  input  [2:0] Address_RB,
  input  clk,
  input  clr,
  input  [31:0] RY,
  output [31:0] RA,
  output [31:0] RB
);

  wire demultiplexer_1_out0, demultiplexer_1_out1, demultiplexer_1_out2, demultiplexer_1_out3,
       demultiplexer_1_out4, demultiplexer_1_out5, demultiplexer_1_out6, demultiplexer_1_out7;
  wire [31:0] R1_q, R2_q, R3_q, R4_q, R5_q, R6_2_q, R6_q, R7_q;

  Demultiplexer #(.select(3)) demultiplexer_1 (
    .out0(demultiplexer_1_out0), .out1(demultiplexer_1_out1), .out2(demultiplexer_1_out2),
    .out3(demultiplexer_1_out3), .out4(demultiplexer_1_out4), .out5(demultiplexer_1_out5),
    .out6(demultiplexer_1_out6), .out7(demultiplexer_1_out7), .in(1'b1), .sel(Address_RY), .en(enRY));
  Register #(.width(32)) R1 (.D(RY), .en(demultiplexer_1_out0), .Q(R1_q), .clk(clk), .clr(clr));
  Register #(.width(32)) R2 (.D(RY), .en(demultiplexer_1_out1), .Q(R2_q), .clk(clk), .clr(clr));
  Register #(.width(32)) R3 (.D(RY), .en(demultiplexer_1_out2), .Q(R3_q), .clk(clk), .clr(clr));
  Register #(.width(32)) R4 (.D(RY), .en(demultiplexer_1_out3), .Q(R4_q), .clk(clk), .clr(clr));
  Register #(.width(32)) R5 (.D(RY), .en(demultiplexer_1_out4), .Q(R5_q), .clk(clk), .clr(clr));
  Register #(.width(32)) R6 (.D(RY), .en(demultiplexer_1_out5), .Q(R6_q), .clk(clk), .clr(clr));
  Register #(.width(32)) R6_2 (.D(RY), .en(demultiplexer_1_out6), .Q(R6_2_q), .clk(clk), .clr(clr));
  Register #(.width(32)) R7 (.D(RY), .en(demultiplexer_1_out7), .Q(R7_q), .clk(clk), .clr(clr));
  Multiplexer #(.select(3), .width(32)) multiplexer_1 (
    .in0(R1_q), .in1(R2_q), .in2(R3_q), .in3(R4_q), .in4(R5_q), .in5(R6_q), .in6(R6_2_q), .in7(R7_q),
    .out(RA), .sel(Address_RA), .en(enRA));
  Multiplexer #(.select(3), .width(32)) multiplexer_2 (
    .in0(R1_q), .in1(R2_q), .in2(R3_q), .in3(R4_q), .in4(R5_q), .in5(R6_q), .in6(R6_2_q), .in7(R7_q),
    .out(RB), .sel(Address_RB), .en(enRB));

  // Notes on the sheet:
  //   19CS01065
  //   Register File
endmodule

module ALU (
  input  [31:0] InputRA,
  input  [31:0] InputRB,
  input  ALU_Enable,
  input  [1:0] ALU_Select,
  output [31:0] ALU_Out
);

  wire [31:0] adder_1_out, and_1_out, or_1_out, subtractor_1_out;

  Adder #(.width(32)) adder_1 (.a(InputRA), .b(InputRB), .out(adder_1_out), .cin(1'b0));  // open: cout
  Subtractor #(.width(32)) subtractor_1 (.a(InputRA), .b(InputRB), .out(subtractor_1_out), .bin(1'b0));  // open: bout
  assign and_1_out = InputRA & InputRB;  // AND_Gate and_1, 32 bits wide
  assign or_1_out = InputRA | InputRB;  // OR_Gate or_1, 32 bits wide
  Multiplexer #(.select(2), .width(32)) multiplexer_1 (
    .in0(adder_1_out), .in1(subtractor_1_out), .in2(and_1_out), .in3(or_1_out), .out(ALU_Out),
    .sel(ALU_Select), .en(ALU_Enable));

  // Notes on the sheet:
  //   19CS01065
  //   ALU
endmodule
